# Fritzing sketch Schematic (saved by Fritzing 0.9.3b)
breadboards: 1

parts:
  U1 = LuaNode32_ESP32
  RHT3 = Humidity and Temperature Sensor RHT03 [part_number=DHT22]
  Grove1 = Grove OLED 128x96
  R3 = Resistor [tolerance=±5% resistance=10k package=THT]
  R4 = Photocell (LDR) [package=THT]
  M1 = HC-SR501_PIR_Sensor_Module [part_number=HC-SR501]
  J1 = Piezo Speaker
  LED1 = smd LED [color="Red (633nm)" package="1206 [SMD]"]
  LED1_2 = smd LED [color="Green (555nm)" package="1206 [SMD]"]
  R7 = Resistor [tolerance=±5% resistance=220 package=THT]
  R8 = Resistor [tolerance=±5% resistance=220 package=THT]
  S2 = Round Pushbutton

nets:
  N1: U1.connector3, R3.Pin_0, R4.pin_1
  N2: U1.connector6, R8.Pin_0
  N3: U1.connector7, LED1_2.anode
  N4: U1.connector8, R7.Pin_0
  N5: U1.connector9, M1.connector1
  N6: U1.connector10, S2.leg0
  N7: U1.connector13, R3.Pin_1, M1.connector2, J1.pin1, LED1.cathode, LED1_2.cathode, S2.leg1
  N8: U1.connector14, R4.pin_0, M1.connector0
  VCC: U1.connector15, RHT3.Vcc, Grove1.VCC
  N9: U1.connector16, RHT3.GND_2, Grove1.GND
  N10: U1.connector19, RHT3.Data-signal
  N11: U1.connector38, Grove1.SDA
  N12: U1.connector41, Grove1.SCL
  N13: J1.pin2, R8.Pin_1
  N14: LED1.anode, R7.Pin_1

notes:
  DHT22
  ESP32
  OLED
  TOMBOL
  LDR
  PIR
  SPEAKER
